# Fritzing sketch temp (saved by Fritzing 0.6.2b)

parts:
  IC1 = IC, DIP package, 8 pins [chip_label=08m spacing=300mil]
  R2 = Resistor [resistance=10k tolerance=±5% package=THT]
  R3 = Resistor [resistance=22k tolerance=±5% package=THT]
  C1 = Ceramic Capacitor [package=THT]
  VCC1 = obsolete Battery
  R4 = Resistor [resistance=270 tolerance=±5% package=THT]
  R5 = Resistor [resistance=270 tolerance=±5% package=THT]
  R6 = Resistor [resistance=270 tolerance=±5% package=THT]
  LED1 = RGB LED (com. cathode, rbg) [package="5 mm [THT]"]
  U1 = mystery part, 3 pins [chip_label=DS18B20 spacing=300mil part_number=DS18B20]
  R7 = Resistor [tolerance=±5% resistance=4.7k package=THT]

nets:
  N1: IC1.pin1, C1.pin_0, VCC1.+, LED1.common_cathode, U1.pin3, R7.Pin_1
  N2: IC1.pin2, R3.Pin_1
  N3: IC1.pin3, R6.Pin_0
  N4: IC1.pin5, R5.Pin_0
  N5: IC1.pin6, R4.Pin_0
  N6: IC1.pin7, U1.pin2, R7.Pin_0
  N7: IC1.pin8, R2.Pin_1, VCC1.-
  N8: R2.Pin_0, R3.Pin_0
  N9: C1.pin_1, U1.pin1
  N10: R4.Pin_1, LED1.red_anode
  N11: R5.Pin_1, LED1.blue_anode
  N12: R6.Pin_1, LED1.green_anode

notes:
  Actually 3 AA batteries
